# Fritzing sketch ultrason_hcsr04 (saved by Fritzing 0.9.2b)
breadboards: 1

parts:
  Composant1 = Arduino Uno (Rev3)
  Composant2 = SRF05 Ultrasonic Rangefinder
  LCD2 = LCD screen

nets:
  N1: Composant1.D9_PWM, Composant2.Trig
  N2: Composant1.D10_PWM/SS, Composant2.Echo
  N3: Composant1.D11_PWM/MOSI, LCD2.E
  N4: Composant1.D12/MISO, LCD2.RS
  N5: Composant1.D2, LCD2.DB7
  N6: Composant1.D3_PWM, LCD2.DB6
  N7: Composant1.D4, LCD2.DB5
  N8: Composant1.D5_PWM, LCD2.DB4
  5V: Composant1.5V, Composant2.VCC, LCD2.VDD
  GND: Composant1.GND, Composant2.GND, LCD2.VSS, LCD2.R/W

// code stored in the sketch: ultrason_hcsr04.ino
//Broches
int trig = 12;
int echo = 11;
long lecture_echo;
long cm;

void setup() {
  // put your setup code here, to run once:
  pinMode(trig,OUTPUT); // Source current
  digitalWrite(trig,LOW); // 0V
  pinMode(echo,INPUT); // Absorb current
  Serial.begin(9600);
}

void loop() {
  // put your main code here, to run repeatedly:
  digitalWrite(trig,HIGH);
  delayMicroseconds(10);
  digitalWrite(trig,LOW);
  lecture_echo = pulseIn(echo,HIGH);
  cm = lecture_echo / 58;
  //Serial.print("Distance en cm : ");
  Serial.println(cm);
  delay(3000);
}

// code stored in the sketch: Untitled2.ino
#include <LiquidCrystal.h>

LiquidCrystal LCD(12,10,11,5,4,3,2);  //Create Liquid Crystal Object called LCD

#define trigPin 13 //Sensor Echo pin connected to Arduino pin 13
#define echoPin 12 //Sensor Trip pin connected to Arduino pin 

void setup() 
{  
  pinMode(trigPin, OUTPUT);
  pinMode(echoPin, INPUT);
  
  LCD.begin(16,2); 
  LCD.setCursor(0,0);  
  LCD.print("Target Distance:");  
}

void loop() {
  long duration, distance;
  digitalWrite(trigPin, LOW);
  delayMicroseconds(2);
  digitalWrite(trigPin, HIGH);
  delayMicroseconds(10);
  digitalWrite(trigPin, LOW);
  duration = pulseIn(echoPin, HIGH);
  distance = (duration/2) / 29.1;

  LCD.setCursor(0,1);  //Set cursor to first column of second row
  LCD.print("                "); //Print blanks to clear the row
  LCD.setCursor(0,1);   //Set Cursor again to first column of second row
  LCD.print(distance); //Print measured distance
  LCD.print(" cm");  //Print your units.
  delay(250); //pause to let things settle
}
